# Fritzing sketch rstft (saved by Fritzing 0.9.2b)

parts:
  J1 = female pin header, 6 pins [form="♀ (female)"]
  R1 = Photocell (LDR) [package=THT]
  R2 = Temperature Sensor (Thermistor) [thermistor_type=NTC package=THT]
  R3 = Resistor [tolerance=±5% resistance=10k package=THT]
  R4 = Resistor [tolerance=±5% resistance=10k package=THT]
  Part1 = Arduino Prototyping Shield
  J2 = female pin header, 6 pins [form="♀ (female)"]
  J3 = rounded female pin header, 10 pins [form="♀ (female rounded)"]

nets:
  N1: J1.pin1, Part1.N$135
  N2: J1.pin2, Part1.N$132
  N3: J1.pin3, Part1.SCL, Part1.N$120, Part1.N$261, J3.pin3
  N4: J1.pin4, Part1.SDA, Part1.N$107, Part1.N$262, J3.pin4
  N5: J1.pin5, R2.pin_1, R4.Pin_1, Part1.+5V, Part1.N$95, Part1.N$230, Part1.N$272, Part1.N$412, J2.pin2, J3.pin1
  N6: J1.pin6, R1.pin_1, R3.Pin_1, Part1.GND, Part1.N$83, Part1.N$245, Part1.N$259, J3.pin2
  N7: R1.pin_0, R4.Pin_0, Part1.N$16, Part1.N$312, Part1.N$319, J2.pin5, J3.pin9
  N8: R3.Pin_0, Part1.N$17, Part1.N$417, Part1.N$421, J2.pin1, J3.pin10
  N9: Part1.N$165, J2.pin3
  N10: Part1.N$263, J3.pin5
  N11: Part1.N$297, J3.pin7
  N12: Part1.N$298, J3.pin6
  N13: Part1.N$299, J3.pin8
  N14: Part1.N$309, J2.pin4
